# Fritzing sketch Schematic (saved by Fritzing 0.9.3b)
breadboards: 1

parts:
  U1 = atmega328 [package=dip]
  XTAL1 = Crystal [frequency="16 Mhz" package=SMD]  # not connected
  C1 = Electrolytic Capacitor [capacitance=1µF package="100 mil [THT, electrolytic]"]
  C3 = Electrolytic Capacitor [capacitance=1µF package="100 mil [THT, electrolytic]"]
  PIR1 = PIR sensor
  T1 = LM35 Temperature Sensor [package="TO92 [THT]"]
  Part1 = IR Receiver Breakout [package=PCB]
  U2 = RELAY-2 [package=relay-g5v]
  R2 = Resistor [tolerance=±5% resistance=220 package=THT]
  R3 = Photocell (LDR) [package=THT]

nets:
  N1: U1.D2, PIR1.SIG
  N2: U1.D3_(PWM), U2.2
  N3: U1.XLAT1, C1.+
  N4: U1.XLAT2, C3.+
  N5: U1.D5_(PWM), T1.Vout
  N6: U1.D7, Part1.OUT
  GND: U1.GND, PIR1.GND
  N7: U1.A0, R2.Pin_0, R3.pin_0
  N8: C1.-, C3.-
  N9: PIR1.VDD, R3.pin_1
